// Logisim project projeto_arcade.circ as structural Verilog
module FlipFlopD (
  input  R,
  input  D,
  input  CK,
  input  S,
  output Q
);

  wire and_1_out, and_2_out, nor_2_out, not_1_out;

  not not_1 (not_1_out, D);
  and and_1 (and_1_out, not_1_out, CK);
  and and_2 (and_2_out, CK, D);
  nor nor_1 (Q, R, and_1_out, nor_2_out);
  nor nor_2 (nor_2_out, Q, and_2_out, S);

  // Notes on the sheet:
  //   Q: pull=down
  //   S: pull=down
  //   CK: pull=down
  //   R: pull=down
  //   D: pull=down
endmodule

module Bit (
  input  R,
  input  D,
  input  CK,
  input  E,
  input  S,
  output Q
);

  wire and_1_out, and_2_out, and_3_out, and_4_out, and_5_out, nor_1_out, nor_2_out, nor_4_out, not_1_out;

  and and_1 (and_1_out, CK, E);
  not not_1 (not_1_out, and_1_out);
  and and_2 (and_2_out, ~D, not_1_out);  // AND_Gate
  and and_3 (and_3_out, not_1_out, D);
  nor nor_1 (nor_1_out, R, and_2_out, nor_2_out);
  nor nor_2 (nor_2_out, nor_1_out, and_3_out, S);
  and and_4 (and_4_out, ~nor_1_out, and_1_out);  // AND_Gate
  and and_5 (and_5_out, and_1_out, nor_1_out);
  nor nor_3 (Q, R, and_4_out, nor_4_out);
  nor nor_4 (nor_4_out, Q, and_5_out, S);

  // Notes on the sheet:
  //   Q: pull=down
  //   D: pull=down
  //   R: pull=down
  //   S: pull=down
  //   CK: pull=down
  //   E: pull=down
endmodule

module Palavra_8b (
  input  [7:0] Data,
  input  CK,
  input  E,
  input  R,
  input  S,
  output [7:0] Out
);

  wire and_1_out, and_2_out, and_3_out, and_4_out, and_5_out, and_6_out, and_7_out, and_8_out, and_9_out,
       and_10_out, and_11_out, and_12_out, and_13_out, and_14_out, and_15_out, and_16_out, and_17_out,
       and_18_out, and_19_out, and_20_out, and_21_out, and_22_out, and_23_out, and_24_out, and_25_out,
       and_26_out, and_27_out, and_28_out, and_29_out, and_30_out, and_31_out, and_32_out, and_33_out,
       and_34_out, and_35_out, and_36_out, and_37_out, and_38_out, and_39_out, and_40_out, nor_1_out,
       nor_2_out, nor_3_out, nor_4_out, nor_5_out, nor_6_out, nor_7_out, nor_8_out, nor_9_out, nor_10_out,
       nor_11_out, nor_12_out, nor_13_out, nor_14_out, nor_15_out, nor_16_out, nor_18_out, nor_20_out,
       nor_22_out, nor_24_out, nor_26_out, nor_28_out, nor_30_out, nor_32_out, not_1_out, not_2_out,
       not_3_out, not_4_out, not_5_out, not_6_out, not_7_out, not_8_out;

  and and_1 (and_1_out, ~Data[0], not_1_out);  // AND_Gate
  not not_1 (not_1_out, and_3_out);
  and and_2 (and_2_out, not_1_out, Data[0]);
  and and_3 (and_3_out, CK, E);
  and and_4 (and_4_out, ~Data[1], not_2_out);  // AND_Gate
  not not_2 (not_2_out, and_6_out);
  and and_5 (and_5_out, not_2_out, Data[1]);
  and and_6 (and_6_out, CK, E);
  and and_7 (and_7_out, ~Data[2], not_3_out);  // AND_Gate
  not not_3 (not_3_out, and_9_out);
  and and_8 (and_8_out, not_3_out, Data[2]);
  and and_9 (and_9_out, CK, E);
  and and_10 (and_10_out, ~Data[3], not_4_out);  // AND_Gate
  and and_11 (and_11_out, not_4_out, Data[3]);
  not not_4 (not_4_out, and_12_out);
  and and_12 (and_12_out, CK, E);
  and and_13 (and_13_out, ~Data[4], not_5_out);  // AND_Gate
  and and_14 (and_14_out, not_5_out, Data[4]);
  not not_5 (not_5_out, and_15_out);
  and and_15 (and_15_out, CK, E);
  and and_16 (and_16_out, ~Data[5], not_6_out);  // AND_Gate
  not not_6 (not_6_out, and_18_out);
  and and_17 (and_17_out, not_6_out, Data[5]);
  and and_18 (and_18_out, CK, E);
  and and_19 (and_19_out, ~Data[6], not_7_out);  // AND_Gate
  and and_20 (and_20_out, not_7_out, Data[6]);
  not not_7 (not_7_out, and_21_out);
  and and_21 (and_21_out, CK, E);
  and and_22 (and_22_out, ~Data[7], not_8_out);  // AND_Gate
  not not_8 (not_8_out, and_24_out);
  and and_23 (and_23_out, not_8_out, Data[7]);
  and and_24 (and_24_out, CK, E);
  nor nor_1 (nor_1_out, R, and_1_out, nor_2_out);
  nor nor_2 (nor_2_out, nor_1_out, and_2_out, S);
  nor nor_3 (nor_3_out, R, and_4_out, nor_4_out);
  nor nor_4 (nor_4_out, nor_3_out, and_5_out, S);
  nor nor_5 (nor_5_out, R, and_7_out, nor_6_out);
  nor nor_6 (nor_6_out, nor_5_out, and_8_out, S);
  nor nor_7 (nor_7_out, R, and_10_out, nor_8_out);
  nor nor_8 (nor_8_out, nor_7_out, and_11_out, S);
  nor nor_9 (nor_9_out, R, and_13_out, nor_10_out);
  nor nor_10 (nor_10_out, nor_9_out, and_14_out, S);
  nor nor_11 (nor_11_out, R, and_16_out, nor_12_out);
  nor nor_12 (nor_12_out, nor_11_out, and_17_out, S);
  nor nor_13 (nor_13_out, R, and_19_out, nor_14_out);
  nor nor_14 (nor_14_out, nor_13_out, and_20_out, S);
  nor nor_15 (nor_15_out, R, and_22_out, nor_16_out);
  nor nor_16 (nor_16_out, nor_15_out, and_23_out, S);
  and and_25 (and_25_out, ~nor_1_out, and_3_out);  // AND_Gate
  and and_26 (and_26_out, and_3_out, nor_1_out);
  and and_27 (and_27_out, ~nor_3_out, and_6_out);  // AND_Gate
  and and_28 (and_28_out, and_6_out, nor_3_out);
  and and_29 (and_29_out, ~nor_5_out, and_9_out);  // AND_Gate
  and and_30 (and_30_out, and_9_out, nor_5_out);
  and and_31 (and_31_out, ~nor_7_out, and_12_out);  // AND_Gate
  and and_32 (and_32_out, and_12_out, nor_7_out);
  and and_33 (and_33_out, ~nor_9_out, and_15_out);  // AND_Gate
  and and_34 (and_34_out, and_15_out, nor_9_out);
  and and_35 (and_35_out, ~nor_11_out, and_18_out);  // AND_Gate
  and and_36 (and_36_out, and_18_out, nor_11_out);
  and and_37 (and_37_out, ~nor_13_out, and_21_out);  // AND_Gate
  and and_38 (and_38_out, and_21_out, nor_13_out);
  and and_39 (and_39_out, ~nor_15_out, and_24_out);  // AND_Gate
  and and_40 (and_40_out, and_24_out, nor_15_out);
  nor nor_17 (Out[0], R, and_25_out, nor_18_out);
  nor nor_18 (nor_18_out, Out[0], and_26_out, S);
  nor nor_19 (Out[1], R, and_27_out, nor_20_out);
  nor nor_20 (nor_20_out, Out[1], and_28_out, S);
  nor nor_21 (Out[2], R, and_29_out, nor_22_out);
  nor nor_22 (nor_22_out, Out[2], and_30_out, S);
  nor nor_23 (Out[3], R, and_31_out, nor_24_out);
  nor nor_24 (nor_24_out, Out[3], and_32_out, S);
  nor nor_25 (Out[4], R, and_33_out, nor_26_out);
  nor nor_26 (nor_26_out, Out[4], and_34_out, S);
  nor nor_27 (Out[5], R, and_35_out, nor_28_out);
  nor nor_28 (nor_28_out, Out[5], and_36_out, S);
  nor nor_29 (Out[6], R, and_37_out, nor_30_out);
  nor nor_30 (nor_30_out, Out[6], and_38_out, S);
  nor nor_31 (Out[7], R, and_39_out, nor_32_out);
  nor nor_32 (nor_32_out, Out[7], and_40_out, S);

  // Notes on the sheet:
  //   E: pull=down
  //   Out: pull=down
  //   S: pull=down
  //   Data: pull=down
  //   CK: pull=down
  //   R: pull=down
endmodule

module Memoria_8x8b (
  input  [2:0] Andress,
  input  [7:0] Data,
  input  Cl,
  input  W,
  input  S,
  input  R,
  output [7:0] Out
);

  wire and_1_out, multi_a_men_8b_1__0, multi_a_men_8b_1__1, multi_a_men_8b_1__2, multi_a_men_8b_1__3,
       multi_a_men_8b_1__4, multi_a_men_8b_1__5, multi_a_men_8b_1__6, multi_a_men_8b_1__7;
  wire [7:0] _0_out, _1_out, _2_out, _3_out, _4_out, _5_out, _6_out, _7_out;

  Multi_A_Men_8b multi_a_men_8b_1 (
    .in_1(Andress), ._0(multi_a_men_8b_1__0), ._1(multi_a_men_8b_1__1), ._2(multi_a_men_8b_1__2),
    ._3(multi_a_men_8b_1__3), ._4(multi_a_men_8b_1__4), ._5(multi_a_men_8b_1__5), ._6(multi_a_men_8b_1__6),
    ._7(multi_a_men_8b_1__7));
  and and_1 (and_1_out, Cl, W);
  Palavra_8b _7 (.Data(Data), .Out(_7_out), .CK(and_1_out), .E(multi_a_men_8b_1__7), .R(R), .S(S));
  Palavra_8b _6 (.Data(Data), .Out(_6_out), .CK(and_1_out), .E(multi_a_men_8b_1__6), .R(R), .S(S));
  Palavra_8b _5 (.Data(Data), .Out(_5_out), .CK(and_1_out), .E(multi_a_men_8b_1__5), .R(R), .S(S));
  Palavra_8b _4 (.Data(Data), .Out(_4_out), .CK(and_1_out), .E(multi_a_men_8b_1__4), .R(R), .S(S));
  Palavra_8b _3 (.Data(Data), .Out(_3_out), .CK(and_1_out), .E(multi_a_men_8b_1__3), .R(R), .S(S));
  Palavra_8b _2 (.Data(Data), .Out(_2_out), .CK(and_1_out), .E(multi_a_men_8b_1__2), .R(R), .S(S));
  Palavra_8b _1 (.Data(Data), .Out(_1_out), .CK(and_1_out), .E(multi_a_men_8b_1__1), .R(R), .S(S));
  Palavra_8b _0 (.Data(Data), .Out(_0_out), .CK(and_1_out), .E(multi_a_men_8b_1__0), .R(R), .S(S));
  Multi_B_Men_8b multi_b_men_8b_1 (
    ._7(_7_out), ._6(_6_out), ._5(_5_out), ._4(_4_out), ._3(_3_out), ._2(_2_out), ._1(_1_out), ._0(_0_out),
    .out_10(Out), .in_1(Andress));

  // Notes on the sheet:
  //   Out: pull=down
  //   R: pull=down
  //   Andress: pull=down
  //   Cl: pull=down
  //   S: pull=down
  //   W: pull=down
  //   Data: pull=down
endmodule

module Multi_A_Men_8b (
  input  [2:0] in_1,
  output _0,
  output _1,
  output _2,
  output _3,
  output _4,
  output _5,
  output _6,
  output _7
);

  and and_1 (_0, ~in_1[2], ~in_1[1], ~in_1[0]);  // AND_Gate
  and and_2 (_1, ~in_1[2], ~in_1[1], in_1[0]);  // AND_Gate
  and and_3 (_2, ~in_1[2], in_1[1], ~in_1[0]);  // AND_Gate
  and and_4 (_3, ~in_1[2], in_1[1], in_1[0]);  // AND_Gate
  and and_5 (_4, in_1[2], ~in_1[1], ~in_1[0]);  // AND_Gate
  and and_6 (_5, in_1[2], ~in_1[1], in_1[0]);  // AND_Gate
  and and_7 (_6, in_1[2], in_1[1], ~in_1[0]);  // AND_Gate
  and and_8 (_7, in_1[2], in_1[1], in_1[0]);

  // Notes on the sheet:
  //   in_1: pull=down
  //   _7: pull=down
  //   _6: pull=down
  //   _0: pull=down
  //   _1: pull=down
  //   _5: pull=down
  //   _3: pull=down
  //   _2: pull=down
  //   _4: pull=down
endmodule

module Multi_B_Men_8b (
  input  [2:0] in_1,
  input  [7:0] _7,
  input  [7:0] _6,
  input  [7:0] _5,
  input  [7:0] _4,
  input  [7:0] _3,
  input  [7:0] _2,
  input  [7:0] _1,
  input  [7:0] _0,
  output [7:0] out_10
);

  wire multi_a_men_8b_1__0, multi_a_men_8b_1__1, multi_a_men_8b_1__2, multi_a_men_8b_1__3,
       multi_a_men_8b_1__4, multi_a_men_8b_1__5, multi_a_men_8b_1__6, multi_a_men_8b_1__7;
  wire [7:0] select_8b_1_out, select_8b_2_out, select_8b_3_out, select_8b_4_out, select_8b_5_out,
       select_8b_6_out, select_8b_7_out, select_8b_8_out;

  Multi_A_Men_8b multi_a_men_8b_1 (
    .in_1(in_1), ._0(multi_a_men_8b_1__0), ._1(multi_a_men_8b_1__1), ._2(multi_a_men_8b_1__2),
    ._3(multi_a_men_8b_1__3), ._4(multi_a_men_8b_1__4), ._5(multi_a_men_8b_1__5), ._6(multi_a_men_8b_1__6),
    ._7(multi_a_men_8b_1__7));
  Select_8b select_8b_1 (.E(multi_a_men_8b_1__7), .In(_7), .Out(select_8b_1_out));
  Select_8b select_8b_2 (.E(multi_a_men_8b_1__6), .In(_6), .Out(select_8b_2_out));
  Select_8b select_8b_3 (.E(multi_a_men_8b_1__5), .In(_5), .Out(select_8b_3_out));
  Select_8b select_8b_4 (.E(multi_a_men_8b_1__4), .In(_4), .Out(select_8b_4_out));
  Select_8b select_8b_5 (.E(multi_a_men_8b_1__3), .In(_3), .Out(select_8b_5_out));
  Select_8b select_8b_6 (.E(multi_a_men_8b_1__2), .In(_2), .Out(select_8b_6_out));
  Select_8b select_8b_7 (.E(multi_a_men_8b_1__1), .In(_1), .Out(select_8b_7_out));
  Select_8b select_8b_8 (.E(multi_a_men_8b_1__0), .In(_0), .Out(select_8b_8_out));
  OR_Men_8b or_men_8b_1 (
    .out_9(out_10), .in_1(select_8b_8_out), .in_2(select_8b_7_out), .in_3(select_8b_6_out),
    .in_4(select_8b_5_out), .in_5(select_8b_4_out), .in_6(select_8b_3_out), .in_7(select_8b_2_out),
    .in_8(select_8b_1_out));

  // Notes on the sheet:
  //   _1: pull=down
  //   in_1: pull=down
  //   _6: pull=down
  //   _4: pull=down
  //   _7: pull=down
  //   _3: pull=down
  //   _2: pull=down
  //   _5: pull=down
  //   out_10: pull=down
  //   _0: pull=down
endmodule

module Select_8b (
  input  E,
  input  [7:0] In,
  output [7:0] Out
);

  and and_1 (Out[0], E, In[0]);
  and and_2 (Out[1], E, In[1]);
  and and_3 (Out[2], E, In[2]);
  and and_4 (Out[3], E, In[3]);
  and and_5 (Out[4], In[4], E);
  and and_6 (Out[5], In[5], E);
  and and_7 (Out[6], In[6], E);
  and and_8 (Out[7], In[7], E);

  // Notes on the sheet:
  //   Out: pull=down
  //   E: pull=down
  //   In: pull=down
endmodule

module OR_Men_8b (
  input  [7:0] in_1,
  input  [7:0] in_2,
  input  [7:0] in_3,
  input  [7:0] in_4,
  input  [7:0] in_5,
  input  [7:0] in_6,
  input  [7:0] in_7,
  input  [7:0] in_8,
  output [7:0] out_9
);

  or or_1 (out_9[0], in_1[0], in_2[0], in_3[0], in_4[0], in_5[0], in_6[0], in_7[0], in_8[0]);
  or or_2 (out_9[1], in_1[1], in_2[1], in_3[1], in_4[1], in_5[1], in_6[1], in_7[1], in_8[1]);
  or or_3 (out_9[2], in_1[2], in_2[2], in_3[2], in_4[2], in_5[2], in_6[2], in_7[2], in_8[2]);
  or or_4 (out_9[3], in_1[3], in_2[3], in_3[3], in_4[3], in_5[3], in_6[3], in_7[3], in_8[3]);
  or or_5 (out_9[4], in_1[4], in_2[4], in_3[4], in_4[4], in_5[4], in_6[4], in_7[4], in_8[4]);
  or or_6 (out_9[5], in_1[5], in_2[5], in_3[5], in_4[5], in_5[5], in_6[5], in_7[5], in_8[5]);
  or or_7 (out_9[6], in_1[6], in_2[6], in_3[6], in_4[6], in_5[6], in_6[6], in_7[6], in_8[6]);
  or or_8 (out_9[7], in_1[7], in_2[7], in_3[7], in_4[7], in_5[7], in_6[7], in_7[7], in_8[7]);

  // Notes on the sheet:
  //   in_5: pull=down
  //   in_2: pull=down
  //   in_6: pull=down
  //   in_3: pull=down
  //   in_1: pull=down
  //   in_7: pull=down
  //   in_4: pull=down
  //   out_9: pull=down
  //   in_8: pull=down
endmodule

module Ctrl_Display_Ate_9 (
  input  [3:0] in_1,
  output _0,
  output _1,
  output _2,
  output _3,
  output _4,
  output _5,
  output _6,
  output _7
);

  wire and_1_out, and_2_out, and_3_out, and_4_out, and_5_out, and_6_out, and_7_out, and_8_out, and_9_out,
       and_10_out, and_11_out, and_12_out, and_13_out, and_14_out, and_15_out, and_16_out;

  and and_1 (and_1_out, ~in_1[1], ~in_1[0]);  // AND_Gate
  and and_2 (and_2_out, in_1[0], in_1[1]);
  and and_3 (and_3_out, ~in_1[2], ~in_1[0]);  // AND_Gate
  and and_4 (and_4_out, in_1[2], in_1[0]);
  and and_5 (and_5_out, ~in_1[1], ~in_1[0]);  // AND_Gate
  and and_6 (and_6_out, in_1[2], ~in_1[1]);  // AND_Gate
  and and_7 (and_7_out, in_1[2], ~in_1[0]);  // AND_Gate
  and and_8 (and_8_out, ~in_1[2], in_1[1]);  // AND_Gate
  and and_9 (and_9_out, in_1[1], ~in_1[0]);  // AND_Gate
  and and_10 (and_10_out, in_1[2], ~in_1[1]);  // AND_Gate
  and and_11 (and_11_out, ~in_1[2], ~in_1[0]);  // AND_Gate
  and and_12 (and_12_out, ~in_1[2], in_1[1]);  // AND_Gate
  and and_13 (and_13_out, in_1[1], ~in_1[0]);  // AND_Gate
  and and_14 (and_14_out, in_1[2], ~in_1[1], in_1[0]);  // AND_Gate
  and and_15 (and_15_out, ~in_1[2], ~in_1[0]);  // AND_Gate
  and and_16 (and_16_out, in_1[1], ~in_1[0]);  // AND_Gate
  or or_1 (_0, and_1_out, ~in_1[2], and_2_out);  // OR_Gate
  or or_2 (_1, in_1[3], in_1[1], and_3_out, and_4_out);
  or or_3 (_2, in_1[3], and_5_out, and_6_out, and_7_out);
  or or_4 (_3, in_1[3], and_8_out, and_9_out, and_10_out);
  or or_5 (_5, ~in_1[1], in_1[0], in_1[2]);  // OR_Gate
  or or_6 (_6, in_1[3], and_11_out, and_12_out, and_13_out, and_14_out);
  or or_7 (_7, and_15_out, and_16_out);
  Button button_1 (.out(_4));

  // Notes on the sheet:
  //   _7: pull=down
  //   _2: pull=down
  //   _5: pull=down
  //   _4: pull=down
  //   in_1: pull=down
  //   _6: pull=down
  //   _3: pull=down
  //   _1: pull=down
  //   _0: pull=down
endmodule

module Add (
  input  A,
  input  B,
  input  Of_in,
  output Of_out,
  output Out
);

  wire and_1_out, and_2_out, and_3_out, and_4_out, and_5_out, and_6_out, and_7_out;

  and and_1 (and_1_out, A, B);
  and and_2 (and_2_out, Of_in, B);
  and and_3 (and_3_out, Of_in, A);
  and and_4 (and_4_out, ~Of_in, ~A, B);  // AND_Gate
  and and_5 (and_5_out, ~Of_in, A, ~B);  // AND_Gate
  and and_6 (and_6_out, Of_in, ~A, ~B);  // AND_Gate
  and and_7 (and_7_out, Of_in, A, B);
  or or_1 (Of_out, and_1_out, and_2_out, and_3_out);
  or or_2 (Out, and_4_out, and_5_out, and_6_out, and_7_out);

  // Notes on the sheet:
  //   Out: pull=down
  //   Of_out: pull=down
  //   A: pull=down
  //   B: pull=down
  //   Of_in: pull=down
endmodule

module Somador (
  input  [7:0] A,
  input  [7:0] B,
  output [7:0] Out
);

  wire add_1_of_out, add_2_of_out, add_3_of_out, add_4_of_out, add_5_of_out, add_6_of_out, add_7_of_out,
       add_8_of_out, button_1_out;

  Button button_1 (.out(button_1_out));
  Add add_1 (.B(B[0]), .A(A[0]), .Of_in(button_1_out), .Of_out(add_1_of_out), .Out(Out[0]));
  Add add_2 (.B(B[1]), .A(A[1]), .Of_in(add_1_of_out), .Of_out(add_2_of_out), .Out(Out[1]));
  Add add_3 (.B(B[2]), .A(A[2]), .Of_in(add_2_of_out), .Of_out(add_3_of_out), .Out(Out[2]));
  Add add_4 (.B(B[3]), .A(A[3]), .Of_in(add_3_of_out), .Of_out(add_4_of_out), .Out(Out[3]));
  Add add_5 (.B(B[5]), .A(A[5]), .Of_in(add_6_of_out), .Of_out(add_5_of_out), .Out(Out[5]));
  Add add_6 (.B(B[4]), .A(A[4]), .Of_in(add_4_of_out), .Of_out(add_6_of_out), .Out(Out[4]));
  Add add_7 (.B(B[6]), .A(A[6]), .Of_in(add_5_of_out), .Of_out(add_7_of_out), .Out(Out[6]));
  Add add_8 (.B(B[7]), .A(A[7]), .Of_in(add_7_of_out), .Of_out(add_8_of_out), .Out(Out[7]));
  LED led_1 (.in(add_8_of_out));

  // Notes on the sheet:
  //   B: pull=down
  //   A: pull=down
  //   Out: pull=down
endmodule

module Ctrl_Display (
  input  [3:0] in_1,
  output _0,
  output _1,
  output _2,
  output _3,
  output _4,
  output _5,
  output _6,
  output _7
);

  wire and_1_out, and_2_out, and_3_out, and_4_out, and_5_out, and_6_out, and_7_out, and_8_out, and_9_out,
       and_10_out, and_11_out, and_12_out, and_13_out, and_14_out, and_15_out, and_16_out, and_17_out,
       and_18_out, and_19_out;

  and and_1 (and_1_out, ~in_1[0], ~in_1[1]);  // AND_Gate
  and and_2 (and_2_out, in_1[0], in_1[1]);
  and and_3 (and_3_out, in_1[0], in_1[2]);
  and and_4 (and_4_out, ~in_1[0], ~in_1[2]);  // AND_Gate
  and and_5 (and_5_out, ~in_1[1], ~in_1[0]);  // AND_Gate
  and and_6 (and_6_out, ~in_1[1], in_1[2]);  // AND_Gate
  and and_7 (and_7_out, in_1[2], ~in_1[0]);  // AND_Gate
  and and_8 (and_8_out, ~in_1[3], ~in_1[2], in_1[1]);  // AND_Gate
  and and_9 (and_9_out, ~in_1[3], ~in_1[0], in_1[1]);  // AND_Gate
  and and_10 (and_10_out, ~in_1[3], ~in_1[1], in_1[2]);  // AND_Gate
  and and_11 (and_11_out, ~in_1[1], ~in_1[2], in_1[3]);  // AND_Gate
  and and_12 (and_12_out, ~in_1[2], ~in_1[0]);  // AND_Gate
  and and_13 (and_13_out, in_1[1], ~in_1[2]);  // AND_Gate
  and and_14 (and_14_out, in_1[1], ~in_1[0]);  // AND_Gate
  and and_15 (and_15_out, in_1[2], ~in_1[1], in_1[0]);  // AND_Gate
  and and_16 (and_16_out, ~in_1[2], ~in_1[0]);  // AND_Gate
  and and_17 (and_17_out, in_1[1], ~in_1[0]);  // AND_Gate
  and and_18 (and_18_out, in_1[3], in_1[1]);
  and and_19 (and_19_out, in_1[3], in_1[2]);
  or or_1 (_0, ~in_1[2], in_1[3], and_1_out, and_2_out);  // OR_Gate
  or or_2 (_1, in_1[1], in_1[3], and_3_out, and_4_out);
  or or_3 (_2, in_1[3], and_5_out, and_6_out, and_7_out);
  or or_4 (_3, and_8_out, and_9_out, and_10_out, and_11_out);
  or or_5 (_5, ~in_1[1], in_1[0], in_1[2], in_1[3]);  // OR_Gate
  or or_6 (_6, in_1[3], and_12_out, and_13_out, and_14_out, and_15_out);
  or or_7 (_7, and_16_out, and_17_out, and_18_out, and_19_out);
  Button button_1 (.out(_4));

  // Notes on the sheet:
  //   _6: pull=down
  //   _0: pull=down
  //   _4: pull=down
  //   _2: pull=down
  //   _7: pull=down
  //   _3: pull=down
  //   in_1: pull=down
  //   _1: pull=down
  //   _5: pull=down
endmodule

module Memoria_16x16b (
  input  S,
  input  R,
  input  Cl,
  input  W,
  input  [15:0] Data,
  input  [3:0] Andress,
  output [15:0] Out
);

  wire and_1_out;
  wire [7:0] multi_a_men_16_1_out_2;
  wire [15:0] _0, _1, _2, _3, _4, _5, _6, _7, _8, _9, A, B, C, D, E, F;
  wire [15:8] multi_a_men_16_1_out_2_2;

  Multi_A_Men_16 multi_a_men_16_1 (.in_1(Andress), .out_2({multi_a_men_16_1_out_2_2, multi_a_men_16_1_out_2}));
  and and_1 (and_1_out, Cl, W);
  Palavra_16b palavra_16b_1 (.Data(Data), .CK(and_1_out), .E(multi_a_men_16_1_out_2[0]), .R(R), .S(S), .Out(_0));
  Palavra_16b palavra_16b_2 (.Data(Data), .CK(and_1_out), .E(multi_a_men_16_1_out_2_2[8]), .R(R), .S(S), .Out(_8));
  Multi_B_Men_16b multi_b_men_16b_1 (
    ._15(F), ._14(E), ._13(D), ._12(C), ._11(B), ._10(A), ._9(_9), ._8(_8), ._7(_7), ._6(_6), ._5(_5),
    ._4(_4), ._3(_3), ._2(_2), ._1(_1), ._0(_0), .Adress(Andress), .Out(Out));
  Palavra_16b palavra_16b_3 (.Data(Data), .CK(and_1_out), .E(multi_a_men_16_1_out_2[1]), .R(R), .S(S), .Out(_1));
  Palavra_16b palavra_16b_4 (.Data(Data), .CK(and_1_out), .E(multi_a_men_16_1_out_2_2[9]), .R(R), .S(S), .Out(_9));
  Palavra_16b palavra_16b_5 (.Data(Data), .CK(and_1_out), .E(multi_a_men_16_1_out_2[2]), .R(R), .S(S), .Out(_2));
  Palavra_16b palavra_16b_6 (.Data(Data), .CK(and_1_out), .E(multi_a_men_16_1_out_2_2[10]), .R(R), .S(S), .Out(A));
  Palavra_16b palavra_16b_7 (.Data(Data), .CK(and_1_out), .E(multi_a_men_16_1_out_2[3]), .R(R), .S(S), .Out(_3));
  Palavra_16b palavra_16b_8 (.Data(Data), .CK(and_1_out), .E(multi_a_men_16_1_out_2_2[11]), .R(R), .S(S), .Out(B));
  Palavra_16b palavra_16b_9 (.Data(Data), .CK(and_1_out), .E(multi_a_men_16_1_out_2[4]), .R(R), .S(S), .Out(_4));
  Palavra_16b palavra_16b_10 (.Data(Data), .CK(and_1_out), .E(multi_a_men_16_1_out_2_2[12]), .R(R), .S(S), .Out(C));
  Palavra_16b palavra_16b_11 (.Data(Data), .CK(and_1_out), .E(multi_a_men_16_1_out_2[5]), .R(R), .S(S), .Out(_5));
  Palavra_16b palavra_16b_12 (.Data(Data), .CK(and_1_out), .E(multi_a_men_16_1_out_2_2[13]), .R(R), .S(S), .Out(D));
  Palavra_16b palavra_16b_13 (.Data(Data), .CK(and_1_out), .E(multi_a_men_16_1_out_2[6]), .R(R), .S(S), .Out(_6));
  Palavra_16b palavra_16b_14 (.Data(Data), .CK(and_1_out), .E(multi_a_men_16_1_out_2_2[14]), .R(R), .S(S), .Out(E));
  Palavra_16b palavra_16b_15 (.Data(Data), .CK(and_1_out), .E(multi_a_men_16_1_out_2[7]), .R(R), .S(S), .Out(_7));
  Palavra_16b palavra_16b_16 (.Data(Data), .CK(and_1_out), .E(multi_a_men_16_1_out_2_2[15]), .R(R), .S(S), .Out(F));

  // Notes on the sheet:
  //   W: pull=down
  //   R: pull=down
  //   S: pull=down
  //   Andress: pull=down
  //   Data: pull=down
  //   Out: pull=down
  //   Cl: pull=down
endmodule

module Palavra_16b (
  input  [15:0] Data,
  input  CK,
  input  E,
  input  R,
  input  S,
  output [15:0] Out
);

  wire and_1_out, and_2_out, and_3_out, and_4_out, and_5_out, and_6_out, and_7_out, and_8_out, and_9_out,
       and_10_out, and_11_out, and_12_out, and_13_out, and_14_out, and_15_out, and_16_out, and_17_out,
       and_18_out, and_19_out, and_20_out, and_21_out, and_22_out, and_23_out, and_24_out, and_25_out,
       and_26_out, and_27_out, and_28_out, and_29_out, and_30_out, and_31_out, and_32_out, and_33_out,
       and_34_out, and_35_out, and_36_out, and_37_out, and_38_out, and_39_out, and_40_out, and_41_out,
       and_42_out, and_43_out, and_44_out, and_45_out, and_46_out, and_47_out, and_48_out, and_49_out,
       and_50_out, and_51_out, and_52_out, and_53_out, and_54_out, and_55_out, and_56_out, and_57_out,
       and_58_out, and_59_out, and_60_out, and_61_out, and_62_out, and_63_out, and_64_out, and_65_out,
       and_66_out, and_67_out, and_68_out, and_69_out, and_70_out, and_71_out, and_72_out, and_73_out,
       and_74_out, and_75_out, and_76_out, and_77_out, and_78_out, and_79_out, and_80_out, nor_1_out,
       nor_2_out, nor_3_out, nor_4_out, nor_5_out, nor_6_out, nor_7_out, nor_8_out, nor_9_out, nor_10_out,
       nor_11_out, nor_12_out, nor_13_out, nor_14_out, nor_15_out, nor_16_out, nor_17_out, nor_18_out,
       nor_19_out, nor_20_out, nor_21_out, nor_22_out, nor_23_out, nor_24_out, nor_25_out, nor_26_out,
       nor_27_out, nor_28_out, nor_29_out, nor_30_out, nor_31_out, nor_32_out, nor_34_out, nor_36_out,
       nor_38_out, nor_40_out, nor_42_out, nor_44_out, nor_46_out, nor_48_out, nor_50_out, nor_52_out,
       nor_54_out, nor_56_out, nor_58_out, nor_60_out, nor_62_out, nor_64_out, not_1_out, not_2_out,
       not_3_out, not_4_out, not_5_out, not_6_out, not_7_out, not_8_out, not_9_out, not_10_out, not_11_out,
       not_12_out, not_13_out, not_14_out, not_15_out, not_16_out;

  not not_1 (not_1_out, and_1_out);
  and and_1 (and_1_out, CK, E);
  not not_2 (not_2_out, and_2_out);
  and and_2 (and_2_out, CK, E);
  not not_3 (not_3_out, and_3_out);
  and and_3 (and_3_out, CK, E);
  not not_4 (not_4_out, and_4_out);
  and and_4 (and_4_out, CK, E);
  not not_5 (not_5_out, and_5_out);
  and and_5 (and_5_out, CK, E);
  not not_6 (not_6_out, and_6_out);
  and and_6 (and_6_out, CK, E);
  and and_7 (and_7_out, ~Data[6], not_7_out);  // AND_Gate
  and and_8 (and_8_out, not_7_out, Data[6]);
  not not_7 (not_7_out, and_9_out);
  and and_9 (and_9_out, CK, E);
  and and_10 (and_10_out, ~Data[7], not_8_out);  // AND_Gate
  and and_11 (and_11_out, not_8_out, Data[7]);
  not not_8 (not_8_out, and_12_out);
  and and_12 (and_12_out, CK, E);
  and and_13 (and_13_out, ~Data[8], not_9_out);  // AND_Gate
  and and_14 (and_14_out, not_9_out, Data[8]);
  not not_9 (not_9_out, and_15_out);
  and and_15 (and_15_out, CK, E);
  and and_16 (and_16_out, ~Data[9], not_10_out);  // AND_Gate
  not not_10 (not_10_out, and_18_out);
  and and_17 (and_17_out, not_10_out, Data[9]);
  and and_18 (and_18_out, CK, E);
  and and_19 (and_19_out, ~Data[10], not_11_out);  // AND_Gate
  not not_11 (not_11_out, and_21_out);
  and and_20 (and_20_out, not_11_out, Data[10]);
  and and_21 (and_21_out, CK, E);
  and and_22 (and_22_out, ~Data[11], not_12_out);  // AND_Gate
  and and_23 (and_23_out, not_12_out, Data[11]);
  not not_12 (not_12_out, and_24_out);
  and and_24 (and_24_out, CK, E);
  and and_25 (and_25_out, ~Data[12], not_13_out);  // AND_Gate
  and and_26 (and_26_out, not_13_out, Data[12]);
  not not_13 (not_13_out, and_27_out);
  and and_27 (and_27_out, CK, E);
  and and_28 (and_28_out, ~Data[13], not_14_out);  // AND_Gate
  and and_29 (and_29_out, not_14_out, Data[13]);
  not not_14 (not_14_out, and_30_out);
  and and_30 (and_30_out, CK, E);
  and and_31 (and_31_out, ~Data[14], not_15_out);  // AND_Gate
  not not_15 (not_15_out, and_33_out);
  and and_32 (and_32_out, not_15_out, Data[14]);
  and and_33 (and_33_out, CK, E);
  and and_34 (and_34_out, ~Data[15], not_16_out);  // AND_Gate
  and and_35 (and_35_out, not_16_out, Data[15]);
  not not_16 (not_16_out, and_36_out);
  and and_36 (and_36_out, CK, E);
  nor nor_1 (nor_1_out, R, and_37_out, nor_2_out);
  and and_37 (and_37_out, ~Data[0], not_1_out);  // AND_Gate
  nor nor_2 (nor_2_out, nor_1_out, and_38_out, S);
  and and_38 (and_38_out, not_1_out, Data[0]);
  nor nor_3 (nor_3_out, R, and_39_out, nor_4_out);
  and and_39 (and_39_out, ~Data[1], not_2_out);  // AND_Gate
  and and_40 (and_40_out, not_2_out, Data[1]);
  nor nor_4 (nor_4_out, nor_3_out, and_40_out, S);
  nor nor_5 (nor_5_out, R, and_41_out, nor_6_out);
  and and_41 (and_41_out, ~Data[2], not_3_out);  // AND_Gate
  nor nor_6 (nor_6_out, nor_5_out, and_42_out, S);
  and and_42 (and_42_out, not_3_out, Data[2]);
  nor nor_7 (nor_7_out, R, and_43_out, nor_8_out);
  and and_43 (and_43_out, ~Data[3], not_4_out);  // AND_Gate
  nor nor_8 (nor_8_out, nor_7_out, and_44_out, S);
  and and_44 (and_44_out, not_4_out, Data[3]);
  nor nor_9 (nor_9_out, R, and_45_out, nor_10_out);
  and and_45 (and_45_out, ~Data[4], not_5_out);  // AND_Gate
  and and_46 (and_46_out, not_5_out, Data[4]);
  nor nor_10 (nor_10_out, nor_9_out, and_46_out, S);
  nor nor_11 (nor_11_out, R, and_47_out, nor_12_out);
  and and_47 (and_47_out, ~Data[5], not_6_out);  // AND_Gate
  nor nor_12 (nor_12_out, nor_11_out, and_48_out, S);
  and and_48 (and_48_out, not_6_out, Data[5]);
  nor nor_13 (nor_13_out, R, and_7_out, nor_14_out);
  nor nor_14 (nor_14_out, nor_13_out, and_8_out, S);
  nor nor_15 (nor_15_out, R, and_10_out, nor_16_out);
  nor nor_16 (nor_16_out, nor_15_out, and_11_out, S);
  nor nor_17 (nor_17_out, R, and_13_out, nor_18_out);
  nor nor_18 (nor_18_out, nor_17_out, and_14_out, S);
  nor nor_19 (nor_19_out, R, and_16_out, nor_20_out);
  nor nor_20 (nor_20_out, nor_19_out, and_17_out, S);
  nor nor_21 (nor_21_out, R, and_19_out, nor_22_out);
  nor nor_22 (nor_22_out, nor_21_out, and_20_out, S);
  nor nor_23 (nor_23_out, R, and_22_out, nor_24_out);
  nor nor_24 (nor_24_out, nor_23_out, and_23_out, S);
  nor nor_25 (nor_25_out, R, and_25_out, nor_26_out);
  nor nor_26 (nor_26_out, nor_25_out, and_26_out, S);
  nor nor_27 (nor_27_out, R, and_28_out, nor_28_out);
  nor nor_28 (nor_28_out, nor_27_out, and_29_out, S);
  nor nor_29 (nor_29_out, R, and_31_out, nor_30_out);
  nor nor_30 (nor_30_out, nor_29_out, and_32_out, S);
  nor nor_31 (nor_31_out, R, and_34_out, nor_32_out);
  nor nor_32 (nor_32_out, nor_31_out, and_35_out, S);
  and and_49 (and_49_out, ~nor_1_out, and_1_out);  // AND_Gate
  and and_50 (and_50_out, and_1_out, nor_1_out);
  and and_51 (and_51_out, ~nor_3_out, and_2_out);  // AND_Gate
  and and_52 (and_52_out, and_2_out, nor_3_out);
  and and_53 (and_53_out, ~nor_5_out, and_3_out);  // AND_Gate
  and and_54 (and_54_out, and_3_out, nor_5_out);
  and and_55 (and_55_out, ~nor_7_out, and_4_out);  // AND_Gate
  and and_56 (and_56_out, and_4_out, nor_7_out);
  and and_57 (and_57_out, ~nor_9_out, and_5_out);  // AND_Gate
  and and_58 (and_58_out, and_5_out, nor_9_out);
  and and_59 (and_59_out, ~nor_11_out, and_6_out);  // AND_Gate
  and and_60 (and_60_out, and_6_out, nor_11_out);
  and and_61 (and_61_out, ~nor_13_out, and_9_out);  // AND_Gate
  and and_62 (and_62_out, and_9_out, nor_13_out);
  and and_63 (and_63_out, ~nor_15_out, and_12_out);  // AND_Gate
  and and_64 (and_64_out, and_12_out, nor_15_out);
  and and_65 (and_65_out, ~nor_17_out, and_15_out);  // AND_Gate
  and and_66 (and_66_out, and_15_out, nor_17_out);
  and and_67 (and_67_out, ~nor_19_out, and_18_out);  // AND_Gate
  and and_68 (and_68_out, and_18_out, nor_19_out);
  and and_69 (and_69_out, ~nor_21_out, and_21_out);  // AND_Gate
  and and_70 (and_70_out, and_21_out, nor_21_out);
  and and_71 (and_71_out, ~nor_23_out, and_24_out);  // AND_Gate
  and and_72 (and_72_out, and_24_out, nor_23_out);
  and and_73 (and_73_out, ~nor_25_out, and_27_out);  // AND_Gate
  and and_74 (and_74_out, and_27_out, nor_25_out);
  and and_75 (and_75_out, ~nor_27_out, and_30_out);  // AND_Gate
  and and_76 (and_76_out, and_30_out, nor_27_out);
  and and_77 (and_77_out, ~nor_29_out, and_33_out);  // AND_Gate
  and and_78 (and_78_out, and_33_out, nor_29_out);
  and and_79 (and_79_out, ~nor_31_out, and_36_out);  // AND_Gate
  and and_80 (and_80_out, and_36_out, nor_31_out);
  nor nor_33 (Out[0], R, and_49_out, nor_34_out);
  nor nor_34 (nor_34_out, Out[0], and_50_out, S);
  nor nor_35 (Out[1], R, and_51_out, nor_36_out);
  nor nor_36 (nor_36_out, Out[1], and_52_out, S);
  nor nor_37 (Out[2], R, and_53_out, nor_38_out);
  nor nor_38 (nor_38_out, Out[2], and_54_out, S);
  nor nor_39 (Out[3], R, and_55_out, nor_40_out);
  nor nor_40 (nor_40_out, Out[3], and_56_out, S);
  nor nor_41 (Out[4], R, and_57_out, nor_42_out);
  nor nor_42 (nor_42_out, Out[4], and_58_out, S);
  nor nor_43 (Out[5], R, and_59_out, nor_44_out);
  nor nor_44 (nor_44_out, Out[5], and_60_out, S);
  nor nor_45 (Out[6], R, and_61_out, nor_46_out);
  nor nor_46 (nor_46_out, Out[6], and_62_out, S);
  nor nor_47 (Out[7], R, and_63_out, nor_48_out);
  nor nor_48 (nor_48_out, Out[7], and_64_out, S);
  nor nor_49 (Out[8], R, and_65_out, nor_50_out);
  nor nor_50 (nor_50_out, Out[8], and_66_out, S);
  nor nor_51 (Out[9], R, and_67_out, nor_52_out);
  nor nor_52 (nor_52_out, Out[9], and_68_out, S);
  nor nor_53 (Out[10], R, and_69_out, nor_54_out);
  nor nor_54 (nor_54_out, Out[10], and_70_out, S);
  nor nor_55 (Out[11], R, and_71_out, nor_56_out);
  nor nor_56 (nor_56_out, Out[11], and_72_out, S);
  nor nor_57 (Out[12], R, and_73_out, nor_58_out);
  nor nor_58 (nor_58_out, Out[12], and_74_out, S);
  nor nor_59 (Out[13], R, and_75_out, nor_60_out);
  nor nor_60 (nor_60_out, Out[13], and_76_out, S);
  nor nor_61 (Out[14], R, and_77_out, nor_62_out);
  nor nor_62 (nor_62_out, Out[14], and_78_out, S);
  nor nor_63 (Out[15], R, and_79_out, nor_64_out);
  nor nor_64 (nor_64_out, Out[15], and_80_out, S);

  // Notes on the sheet:
  //   E: pull=down
  //   R: pull=down
  //   CK: pull=down
  //   Out: pull=down
  //   Data: pull=down
  //   S: pull=down
endmodule

module Multi_A_Men_16 (
  input  [3:0] in_1,
  output [15:0] out_2
);

  and and_1 (out_2[0], ~in_1[3], ~in_1[2], ~in_1[1], ~in_1[0]);  // AND_Gate
  and and_2 (out_2[1], ~in_1[3], ~in_1[2], ~in_1[1], in_1[0]);  // AND_Gate
  and and_3 (out_2[2], ~in_1[3], ~in_1[2], in_1[1], ~in_1[0]);  // AND_Gate
  and and_4 (out_2[3], ~in_1[3], ~in_1[2], in_1[1], in_1[0]);  // AND_Gate
  and and_5 (out_2[4], ~in_1[3], in_1[2], ~in_1[1], ~in_1[0]);  // AND_Gate
  and and_6 (out_2[5], ~in_1[3], in_1[2], ~in_1[1], in_1[0]);  // AND_Gate
  and and_7 (out_2[6], ~in_1[3], in_1[2], in_1[1], ~in_1[0]);  // AND_Gate
  and and_8 (out_2[7], ~in_1[3], in_1[2], in_1[1], in_1[0]);  // AND_Gate
  and and_9 (out_2[8], in_1[3], ~in_1[2], ~in_1[1], ~in_1[0]);  // AND_Gate
  and and_10 (out_2[9], in_1[3], ~in_1[2], ~in_1[1], in_1[0]);  // AND_Gate
  and and_11 (out_2[10], in_1[3], ~in_1[2], in_1[1], ~in_1[0]);  // AND_Gate
  and and_12 (out_2[11], in_1[3], ~in_1[2], in_1[1], in_1[0]);  // AND_Gate
  and and_13 (out_2[12], in_1[3], in_1[2], ~in_1[1], ~in_1[0]);  // AND_Gate
  and and_14 (out_2[13], in_1[3], in_1[2], ~in_1[1], in_1[0]);  // AND_Gate
  and and_15 (out_2[14], in_1[3], in_1[2], in_1[1], ~in_1[0]);  // AND_Gate
  and and_16 (out_2[15], in_1[3], in_1[2], in_1[1], in_1[0]);

  // Notes on the sheet:
  //   in_1: pull=down
  //   out_2: pull=down
endmodule

module Select_16b (
  input  E,
  input  [15:0] In,
  output [15:0] Out
);

  and and_1 (Out[0], E, In[0]);
  and and_2 (Out[1], E, In[1]);
  and and_3 (Out[2], E, In[2]);
  and and_4 (Out[3], E, In[3]);
  and and_5 (Out[4], E, In[4]);
  and and_6 (Out[5], E, In[5]);
  and and_7 (Out[6], E, In[6]);
  and and_8 (Out[7], E, In[7]);
  and and_9 (Out[8], In[8], E);
  and and_10 (Out[9], In[9], E);
  and and_11 (Out[10], In[10], E);
  and and_12 (Out[11], In[11], E);
  and and_13 (Out[12], In[12], E);
  and and_14 (Out[13], In[13], E);
  and and_15 (Out[14], In[14], E);
  and and_16 (Out[15], In[15], E);

  // Notes on the sheet:
  //   Out: pull=down
  //   In: pull=down
  //   E: pull=down
endmodule

module Multi_B_Men_16b (
  input  [3:0] Adress,
  input  [15:0] _15,
  input  [15:0] _14,
  input  [15:0] _13,
  input  [15:0] _12,
  input  [15:0] _11,
  input  [15:0] _10,
  input  [15:0] _9,
  input  [15:0] _8,
  input  [15:0] _7,
  input  [15:0] _6,
  input  [15:0] _5,
  input  [15:0] _4,
  input  [15:0] _3,
  input  [15:0] _2,
  input  [15:0] _1,
  input  [15:0] _0,
  output [15:0] Out
);

  wire [15:0] multi_a_men_16_1_out_2, select_16b_1_out, select_16b_2_out, select_16b_3_out, select_16b_4_out,
       select_16b_5_out, select_16b_6_out, select_16b_7_out, select_16b_8_out, select_16b_9_out,
       select_16b_10_out, select_16b_11_out, select_16b_12_out, select_16b_13_out, select_16b_14_out,
       select_16b_15_out, select_16b_16_out;

  Multi_A_Men_16 multi_a_men_16_1 (.in_1(Adress), .out_2(multi_a_men_16_1_out_2));
  Select_16b select_16b_1 (.In(_15), .Out(select_16b_1_out), .E(multi_a_men_16_1_out_2[15]));
  Select_16b select_16b_2 (.In(_14), .Out(select_16b_2_out), .E(multi_a_men_16_1_out_2[14]));
  Select_16b select_16b_3 (.In(_13), .Out(select_16b_3_out), .E(multi_a_men_16_1_out_2[13]));
  Select_16b select_16b_4 (.In(_12), .Out(select_16b_4_out), .E(multi_a_men_16_1_out_2[12]));
  Select_16b select_16b_5 (.In(_11), .Out(select_16b_5_out), .E(multi_a_men_16_1_out_2[11]));
  Select_16b select_16b_6 (.In(_10), .Out(select_16b_6_out), .E(multi_a_men_16_1_out_2[10]));
  Select_16b select_16b_7 (.In(_9), .Out(select_16b_7_out), .E(multi_a_men_16_1_out_2[9]));
  Select_16b select_16b_8 (.In(_8), .Out(select_16b_8_out), .E(multi_a_men_16_1_out_2[8]));
  Select_16b select_16b_9 (.In(_7), .Out(select_16b_9_out), .E(multi_a_men_16_1_out_2[7]));
  Select_16b select_16b_10 (.In(_6), .Out(select_16b_10_out), .E(multi_a_men_16_1_out_2[6]));
  Select_16b select_16b_11 (.In(_5), .Out(select_16b_11_out), .E(multi_a_men_16_1_out_2[5]));
  Select_16b select_16b_12 (.In(_4), .Out(select_16b_12_out), .E(multi_a_men_16_1_out_2[4]));
  Select_16b select_16b_13 (.In(_3), .Out(select_16b_13_out), .E(multi_a_men_16_1_out_2[3]));
  Select_16b select_16b_14 (.In(_2), .Out(select_16b_14_out), .E(multi_a_men_16_1_out_2[2]));
  Select_16b select_16b_15 (.In(_1), .Out(select_16b_15_out), .E(multi_a_men_16_1_out_2[1]));
  Select_16b select_16b_16 (.In(_0), .Out(select_16b_16_out), .E(multi_a_men_16_1_out_2[0]));
  OR_Men_16b or_men_16b_1 (
    ._15(select_16b_1_out), ._14(select_16b_2_out), ._13(select_16b_3_out), ._12(select_16b_4_out),
    ._11(select_16b_5_out), ._10(select_16b_6_out), ._9(select_16b_7_out), ._8(select_16b_8_out),
    ._7(select_16b_9_out), ._6(select_16b_10_out), ._5(select_16b_11_out), ._4(select_16b_12_out),
    ._3(select_16b_13_out), ._2(select_16b_14_out), ._1(select_16b_15_out), ._0(select_16b_16_out),
    .out_17(Out));

  // Notes on the sheet:
  //   _10: pull=down
  //   _4: pull=down
  //   Out: pull=down
  //   _5: pull=down
  //   _15: pull=down
  //   _9: pull=down
  //   _0: pull=down
  //   _2: pull=down
  //   _6: pull=down
  //   _8: pull=down
  //   _12: pull=down
  //   _13: pull=down
  //   _14: pull=down
  //   _11: pull=down
  //   Adress: pull=down
  //   _3: pull=down
  //   _1: pull=down
  //   _7: pull=down
endmodule

module OR_Men_16b (
  input  [15:0] _15,
  input  [15:0] _14,
  input  [15:0] _13,
  input  [15:0] _12,
  input  [15:0] _11,
  input  [15:0] _10,
  input  [15:0] _9,
  input  [15:0] _8,
  input  [15:0] _7,
  input  [15:0] _6,
  input  [15:0] _5,
  input  [15:0] _4,
  input  [15:0] _3,
  input  [15:0] _2,
  input  [15:0] _1,
  input  [15:0] _0,
  output [15:0] out_17
);

  assign out_17 = _15 | _14 | _13 | _12 | _11 | _10 | _9 | _8 | _7 | _6 | _5 | _4 | _3 | _2 | _1 | _0;  // OR_Gate or_1, 16 bits wide

  // Notes on the sheet:
  //   _11: pull=down
  //   _5: pull=down
  //   _13: pull=down
  //   _3: pull=down
  //   _12: pull=down
  //   _7: pull=down
  //   _1: pull=down
  //   _4: pull=down
  //   _2: pull=down
  //   _15: pull=down
  //   _6: pull=down
  //   _0: pull=down
  //   _9: pull=down
  //   _14: pull=down
  //   out_17: pull=down
  //   _8: pull=down
  //   _10: pull=down
endmodule

module Contador (
  input  Start,
  input  [7:0] in_2,
  input  in_3,
  input  [15:0] in_4,
  input  [2:0] in_5
);

  wire and_1_out, button_1_out, button_2_out, clock_1_out, R_out, S_out;
  wire [2:0] or_1_out;
  wire [7:0] Add, ctrl_display_d_1_out_2, ctrl_display_u_1_out_2, somador_1_out;
  wire [15:0] memoria_8x16b_1_out;

  Clock clock_1 (.out(clock_1_out));
  Button R (.out(R_out));
  Button S (.out(S_out));
  assign or_1_out = in_5 | Add[2:0];  // OR_Gate or_1, 3 bits wide
  and and_1 (and_1_out, clock_1_out, Start);
  Memoria_8x16b memoria_8x16b_1 (
    .S(S_out), .R(R_out), .Cl(clock_1_out), .W(in_3), .Data(in_4), .Andress(or_1_out),
    .Out(memoria_8x16b_1_out));
  Button button_1 (.out(button_1_out));
  Button button_2 (.out(button_2_out));
  Palavra_8b palavra_8b_1 (
    .Data(somador_1_out), .Out(Add), .CK(and_1_out), .E(and_1_out), .R(button_2_out), .S(button_1_out));
  Somador somador_1 (.A(Add), .B(in_2), .Out(somador_1_out));
  DotMatrix #(.inputtype("row"), .matrixcols(4), .matrixrows(4)) dotmatrix_1 (
    .row0(memoria_8x16b_1_out[3:0]), .row1(memoria_8x16b_1_out[7:4]), .row2(memoria_8x16b_1_out[11:8]),
    .row3(memoria_8x16b_1_out[15:12]));
  Ctrl_Display_U ctrl_display_u_1 (.in_1(somador_1_out[3:0]), .out_2(ctrl_display_u_1_out_2));
  Ctrl_Display_D ctrl_display_d_1 (.in_1(somador_1_out[3:0]), .out_2(ctrl_display_d_1_out_2));
  _7_Segment_Display u_7_segment_display_1 (
    .g(ctrl_display_u_1_out_2[3]), .f(ctrl_display_u_1_out_2[2]), .a(ctrl_display_u_1_out_2[1]),
    .b(ctrl_display_u_1_out_2[0]), .e(ctrl_display_u_1_out_2[7]), .d(ctrl_display_u_1_out_2[6]),
    .c(ctrl_display_u_1_out_2[5]), .dp(ctrl_display_u_1_out_2[4]));
  _7_Segment_Display u_7_segment_display_2 (
    .g(ctrl_display_d_1_out_2[3]), .f(ctrl_display_d_1_out_2[2]), .a(ctrl_display_d_1_out_2[1]),
    .b(ctrl_display_d_1_out_2[0]), .e(ctrl_display_d_1_out_2[7]), .d(ctrl_display_d_1_out_2[6]),
    .c(ctrl_display_d_1_out_2[5]), .dp(ctrl_display_d_1_out_2[4]));

  // Notes on the sheet:
  //   in_4: pull=down
  //   in_2: pull=down
endmodule

module Ctrl_Display_U (
  input  [3:0] in_1,
  output [7:0] out_2
);

  wire and_1_out, and_2_out, and_3_out, and_4_out, and_5_out, and_6_out, and_7_out, and_8_out, and_9_out,
       and_10_out, and_11_out, and_12_out, and_13_out, and_14_out, and_15_out, and_16_out, and_17_out,
       and_18_out, and_19_out, and_20_out, and_21_out, and_22_out, and_23_out, and_24_out, and_25_out,
       and_26_out, and_27_out, and_28_out, and_29_out, and_30_out, and_31_out;

  and and_1 (and_1_out, ~in_1[1], ~in_1[0]);  // AND_Gate
  and and_2 (and_2_out, in_1[3], ~in_1[1]);  // AND_Gate
  and and_3 (and_3_out, in_1[3], ~in_1[0]);  // AND_Gate
  and and_4 (and_4_out, ~in_1[3], in_1[1], in_1[0]);  // AND_Gate
  and and_5 (and_5_out, ~in_1[2], ~in_1[0]);  // AND_Gate
  and and_6 (and_6_out, ~in_1[3], in_1[1]);  // AND_Gate
  and and_7 (and_7_out, in_1[2], in_1[0]);
  and and_8 (and_8_out, in_1[3], ~in_1[1]);  // AND_Gate
  and and_9 (and_9_out, ~in_1[3], ~in_1[1], ~in_1[0]);  // AND_Gate
  and and_10 (and_10_out, ~in_1[3], in_1[2], ~in_1[1]);  // AND_Gate
  and and_11 (and_11_out, ~in_1[3], in_1[2], ~in_1[0]);  // AND_Gate
  and and_12 (and_12_out, in_1[3], ~in_1[2], ~in_1[1]);  // AND_Gate
  and and_13 (and_13_out, in_1[3], ~in_1[2], ~in_1[0]);  // AND_Gate
  and and_14 (and_14_out, in_1[3], in_1[2], in_1[1]);
  and and_15 (and_15_out, in_1[2], ~in_1[1]);  // AND_Gate
  and and_16 (and_16_out, in_1[2], ~in_1[0]);  // AND_Gate
  and and_17 (and_17_out, in_1[3], ~in_1[1]);  // AND_Gate
  and and_18 (and_18_out, in_1[3], in_1[2]);
  and and_19 (and_19_out, ~in_1[3], ~in_1[2], in_1[1]);  // AND_Gate
  and and_20 (and_20_out, ~in_1[3], ~in_1[1]);  // AND_Gate
  and and_21 (and_21_out, in_1[2], in_1[1]);
  and and_22 (and_22_out, in_1[3], ~in_1[2]);  // AND_Gate
  and and_23 (and_23_out, ~in_1[2], ~in_1[0]);  // AND_Gate
  and and_24 (and_24_out, in_1[3], ~in_1[1]);  // AND_Gate
  and and_25 (and_25_out, ~in_1[3], ~in_1[2], in_1[1]);  // AND_Gate
  and and_26 (and_26_out, ~in_1[3], in_1[1], ~in_1[0]);  // AND_Gate
  and and_27 (and_27_out, in_1[2], ~in_1[1], in_1[0]);  // AND_Gate
  and and_28 (and_28_out, in_1[3], in_1[2], in_1[0]);
  and and_29 (and_29_out, ~in_1[2], ~in_1[0]);  // AND_Gate
  and and_30 (and_30_out, ~in_1[3], in_1[1], ~in_1[0]);  // AND_Gate
  and and_31 (and_31_out, in_1[3], ~in_1[1], ~in_1[0]);  // AND_Gate
  or or_1 (out_2[0], ~in_1[2], and_1_out, and_2_out, and_3_out, and_4_out);  // OR_Gate
  or or_2 (out_2[1], and_5_out, and_6_out, and_7_out, and_8_out);
  or or_3 (out_2[3], and_15_out, and_16_out, and_17_out, and_18_out, and_19_out);
  or or_4 (out_2[5], in_1[0], and_20_out, and_21_out, and_22_out);
  or or_5 (out_2[7], and_29_out, and_30_out, and_31_out);
  not not_1 (out_2[4], 1'b1);
  or or_6 (out_2[2], and_9_out, and_10_out, and_11_out, and_12_out, and_13_out, and_14_out);
  or or_7 (out_2[6], and_23_out, and_24_out, and_25_out, and_26_out, and_27_out, and_28_out);

  // Notes on the sheet:
  //   out_2: pull=down
  //   in_1: pull=down
endmodule

module Ctrl_Display_D (
  input  [3:0] in_1,
  output [7:0] out_2
);

  wire and_1_out;

  and and_1 (and_1_out, ~in_1[2], ~in_1[1]);  // AND_Gate
  or or_1 (out_2[7], and_1_out, ~in_1[3]);  // OR_Gate
  not not_1 (out_2[3], 1'b1);
  not not_2 (out_2[4], 1'b1);

  assign {out_2[6:5], out_2[2:0]} = {out_2[7], 1'b1, {2{out_2[7]}}, 1'b1};

  // Notes on the sheet:
  //   out_2: pull=down
  //   in_1: pull=down
endmodule

module Memoria_8x16b (
  input  S,
  input  R,
  input  Cl,
  input  W,
  input  [15:0] Data,
  input  [2:0] Andress,
  output [15:0] Out
);

  wire and_1_out, multi_a_men_8b_1__0, multi_a_men_8b_1__1, multi_a_men_8b_1__2, multi_a_men_8b_1__3,
       multi_a_men_8b_1__4, multi_a_men_8b_1__5, multi_a_men_8b_1__6, multi_a_men_8b_1__7;
  wire [15:0] _0, _1, _2, _3, _4, _5, _6, _7, select_16b_1_out, select_16b_2_out, select_16b_3_out,
       select_16b_4_out, select_16b_5_out, select_16b_6_out, select_16b_7_out, select_16b_8_out;

  and and_1 (and_1_out, Cl, W);
  Multi_A_Men_8b multi_a_men_8b_1 (
    .in_1(Andress), ._0(multi_a_men_8b_1__0), ._1(multi_a_men_8b_1__1), ._2(multi_a_men_8b_1__2),
    ._3(multi_a_men_8b_1__3), ._4(multi_a_men_8b_1__4), ._5(multi_a_men_8b_1__5), ._6(multi_a_men_8b_1__6),
    ._7(multi_a_men_8b_1__7));
  Palavra_16b palavra_16b_1 (.Data(Data), .CK(and_1_out), .E(multi_a_men_8b_1__0), .R(R), .S(S), .Out(_0));
  Select_16b select_16b_1 (.In(_0), .Out(select_16b_1_out), .E(multi_a_men_8b_1__0));
  Select_16b select_16b_2 (.In(_1), .Out(select_16b_2_out), .E(multi_a_men_8b_1__1));
  Select_16b select_16b_3 (.In(_2), .Out(select_16b_3_out), .E(multi_a_men_8b_1__2));
  Select_16b select_16b_4 (.In(_3), .Out(select_16b_4_out), .E(multi_a_men_8b_1__3));
  Palavra_16b palavra_16b_2 (.Data(Data), .CK(and_1_out), .E(multi_a_men_8b_1__1), .R(R), .S(S), .Out(_1));
  Select_16b select_16b_5 (.In(_4), .Out(select_16b_5_out), .E(multi_a_men_8b_1__4));
  Select_16b select_16b_6 (.In(_5), .Out(select_16b_6_out), .E(multi_a_men_8b_1__5));
  Palavra_16b palavra_16b_3 (.Data(Data), .CK(and_1_out), .E(multi_a_men_8b_1__2), .R(R), .S(S), .Out(_2));
  Select_16b select_16b_7 (.In(_6), .Out(select_16b_7_out), .E(multi_a_men_8b_1__6));
  Select_16b select_16b_8 (.In(_7), .Out(select_16b_8_out), .E(multi_a_men_8b_1__7));
  assign Out = select_16b_8_out | select_16b_7_out | select_16b_6_out | select_16b_5_out | select_16b_4_out | select_16b_3_out | select_16b_2_out | select_16b_1_out;  // OR_Gate or_1, 16 bits wide
  Palavra_16b palavra_16b_4 (.Data(Data), .CK(and_1_out), .E(multi_a_men_8b_1__3), .R(R), .S(S), .Out(_3));
  Palavra_16b palavra_16b_5 (.Data(Data), .CK(and_1_out), .E(multi_a_men_8b_1__4), .R(R), .S(S), .Out(_4));
  Palavra_16b palavra_16b_6 (.Data(Data), .CK(and_1_out), .E(multi_a_men_8b_1__5), .R(R), .S(S), .Out(_5));
  Palavra_16b palavra_16b_7 (.Data(Data), .CK(and_1_out), .E(multi_a_men_8b_1__6), .R(R), .S(S), .Out(_6));
  Palavra_16b palavra_16b_8 (.Data(Data), .CK(and_1_out), .E(multi_a_men_8b_1__7), .R(R), .S(S), .Out(_7));

  // Notes on the sheet:
  //   R: pull=down
  //   Out: pull=down
  //   S: pull=down
  //   Data: pull=down
  //   Cl: pull=down
  //   Andress: pull=down
  //   W: pull=down
endmodule
